// Logisim project 4bitRAM.circ as structural Verilog: 1 circuit, main circuit main
module main (
  input  Data_Input,
  input  in_2,
  input  in_3,
  input  in_4,
  input  Mode,
  input  Address,
  input  in_7
);

  wire and_1_out, and_2_out, and_3_out, and_4_out, and_5_out, and_6_out, and_7_out, and_8_out, and_9_out,
       and_10_out, and_11_out, and_12_out, and_13_out, and_14_out, and_15_out, and_16_out, and_17_out,
       and_18_out, and_19_out, and_20_out, and_21_out, and_22_out, and_23_out, and_24_out, and_25_out,
       and_26_out, and_27_out, and_28_out, and_29_out, and_30_out, and_31_out, and_32_out, and_33_out,
       and_34_out, and_35_out, and_36_out, controlled_buffer_1_out, controlled_buffer_5_out,
       controlled_buffer_9_out, controlled_buffer_13_out, decoder_1_out0, decoder_1_out1, decoder_1_out2,
       decoder_1_out3, nor_1_out, nor_2_out, nor_3_out, nor_4_out, nor_5_out, nor_6_out, nor_7_out,
       nor_8_out, nor_9_out, nor_10_out, nor_11_out, nor_12_out, nor_13_out, nor_14_out, nor_15_out,
       nor_16_out, nor_17_out, nor_18_out, nor_19_out, nor_20_out, nor_21_out, nor_22_out, nor_23_out,
       nor_24_out, nor_25_out, nor_26_out, nor_27_out, nor_28_out, nor_29_out, nor_30_out, nor_31_out,
       nor_32_out, not_1_out, not_2_out, not_3_out, not_4_out, not_5_out, not_6_out, not_7_out, not_8_out,
       not_9_out, not_10_out, not_11_out, not_12_out, not_13_out, not_14_out, not_15_out, not_16_out;

  Decoder #(.enable("false"), .select(2)) decoder_1 (
    .out0(decoder_1_out0), .out1(decoder_1_out1), .out2(decoder_1_out2), .out3(decoder_1_out3),
    .sel({in_7, Address}));
  and and_1 (and_1_out, decoder_1_out0, Mode);
  and and_2 (and_2_out, decoder_1_out1, Mode);
  and and_3 (and_3_out, decoder_1_out2, Mode);
  and and_4 (and_4_out, decoder_1_out3, Mode);
  and and_5 (and_5_out, and_1_out, not_1_out);
  not not_1 (not_1_out, Data_Input);
  and and_6 (and_6_out, and_1_out, Data_Input);
  and and_7 (and_7_out, and_2_out, not_2_out);
  not not_2 (not_2_out, Data_Input);
  and and_8 (and_8_out, and_2_out, Data_Input);
  and and_9 (and_9_out, and_3_out, not_3_out);
  not not_3 (not_3_out, Data_Input);
  and and_10 (and_10_out, and_3_out, Data_Input);
  and and_11 (and_11_out, and_4_out, not_4_out);
  not not_4 (not_4_out, Data_Input);
  and and_12 (and_12_out, and_4_out, Data_Input);
  nor nor_1 (nor_1_out, and_5_out, nor_2_out);
  nor nor_2 (nor_2_out, nor_1_out, and_6_out);
  nor nor_3 (nor_3_out, and_7_out, nor_4_out);
  nor nor_4 (nor_4_out, nor_3_out, and_8_out);
  nor nor_5 (nor_5_out, and_9_out, nor_6_out);
  nor nor_6 (nor_6_out, nor_5_out, and_10_out);
  nor nor_7 (nor_7_out, and_11_out, nor_8_out);
  nor nor_8 (nor_8_out, nor_7_out, and_12_out);
  assign controlled_buffer_1_out = decoder_1_out0 ? nor_1_out : 1'bz;  // Controlled_Buffer controlled_buffer_1
  assign controlled_buffer_1_out = decoder_1_out1 ? nor_3_out : 1'bz;  // Controlled_Buffer controlled_buffer_2
  assign controlled_buffer_1_out = decoder_1_out2 ? nor_5_out : 1'bz;  // Controlled_Buffer controlled_buffer_3
  assign controlled_buffer_1_out = decoder_1_out3 ? nor_7_out : 1'bz;  // Controlled_Buffer controlled_buffer_4
  LED led_1 (.in(controlled_buffer_1_out));
  not not_5 (not_5_out, in_2);
  not not_6 (not_6_out, in_2);
  not not_7 (not_7_out, in_2);
  not not_8 (not_8_out, in_2);
  and and_13 (and_13_out, and_1_out, not_5_out);
  and and_14 (and_14_out, and_1_out, in_2);
  and and_15 (and_15_out, and_2_out, not_6_out);
  and and_16 (and_16_out, and_2_out, in_2);
  and and_17 (and_17_out, and_3_out, not_7_out);
  and and_18 (and_18_out, and_3_out, in_2);
  and and_19 (and_19_out, and_4_out, not_8_out);
  and and_20 (and_20_out, and_4_out, in_2);
  nor nor_9 (nor_9_out, and_13_out, nor_10_out);
  nor nor_10 (nor_10_out, nor_9_out, and_14_out);
  nor nor_11 (nor_11_out, and_15_out, nor_12_out);
  nor nor_12 (nor_12_out, nor_11_out, and_16_out);
  nor nor_13 (nor_13_out, and_17_out, nor_14_out);
  nor nor_14 (nor_14_out, nor_13_out, and_18_out);
  nor nor_15 (nor_15_out, and_19_out, nor_16_out);
  nor nor_16 (nor_16_out, nor_15_out, and_20_out);
  assign controlled_buffer_5_out = decoder_1_out0 ? nor_9_out : 1'bz;  // Controlled_Buffer controlled_buffer_5
  assign controlled_buffer_5_out = decoder_1_out1 ? nor_11_out : 1'bz;  // Controlled_Buffer controlled_buffer_6
  assign controlled_buffer_5_out = decoder_1_out2 ? nor_13_out : 1'bz;  // Controlled_Buffer controlled_buffer_7
  assign controlled_buffer_5_out = decoder_1_out3 ? nor_15_out : 1'bz;  // Controlled_Buffer controlled_buffer_8
  LED led_2 (.in(controlled_buffer_5_out));
  not not_9 (not_9_out, in_3);
  not not_10 (not_10_out, in_3);
  not not_11 (not_11_out, in_3);
  not not_12 (not_12_out, in_3);
  and and_21 (and_21_out, and_1_out, not_9_out);
  and and_22 (and_22_out, and_1_out, in_3);
  and and_23 (and_23_out, and_2_out, not_10_out);
  and and_24 (and_24_out, and_2_out, in_3);
  and and_25 (and_25_out, and_3_out, not_11_out);
  and and_26 (and_26_out, and_3_out, in_3);
  and and_27 (and_27_out, and_4_out, not_12_out);
  and and_28 (and_28_out, and_4_out, in_3);
  nor nor_17 (nor_17_out, and_21_out, nor_18_out);
  nor nor_18 (nor_18_out, nor_17_out, and_22_out);
  nor nor_19 (nor_19_out, and_23_out, nor_20_out);
  nor nor_20 (nor_20_out, nor_19_out, and_24_out);
  nor nor_21 (nor_21_out, and_25_out, nor_22_out);
  nor nor_22 (nor_22_out, nor_21_out, and_26_out);
  nor nor_23 (nor_23_out, and_27_out, nor_24_out);
  nor nor_24 (nor_24_out, nor_23_out, and_28_out);
  assign controlled_buffer_9_out = decoder_1_out0 ? nor_17_out : 1'bz;  // Controlled_Buffer controlled_buffer_9
  assign controlled_buffer_9_out = decoder_1_out1 ? nor_19_out : 1'bz;  // Controlled_Buffer controlled_buffer_10
  assign controlled_buffer_9_out = decoder_1_out2 ? nor_21_out : 1'bz;  // Controlled_Buffer controlled_buffer_11
  assign controlled_buffer_9_out = decoder_1_out3 ? nor_23_out : 1'bz;  // Controlled_Buffer controlled_buffer_12
  LED led_3 (.in(controlled_buffer_9_out));
  not not_13 (not_13_out, in_4);
  not not_14 (not_14_out, in_4);
  not not_15 (not_15_out, in_4);
  not not_16 (not_16_out, in_4);
  and and_29 (and_29_out, and_1_out, not_13_out);
  and and_30 (and_30_out, and_1_out, in_4);
  and and_31 (and_31_out, and_2_out, not_14_out);
  and and_32 (and_32_out, and_2_out, in_4);
  and and_33 (and_33_out, and_3_out, not_15_out);
  and and_34 (and_34_out, and_3_out, in_4);
  and and_35 (and_35_out, and_4_out, not_16_out);
  and and_36 (and_36_out, and_4_out, in_4);
  nor nor_25 (nor_25_out, and_29_out, nor_26_out);
  assign controlled_buffer_13_out = decoder_1_out0 ? nor_25_out : 1'bz;  // Controlled_Buffer controlled_buffer_13
  nor nor_26 (nor_26_out, nor_25_out, and_30_out);
  nor nor_27 (nor_27_out, and_31_out, nor_28_out);
  assign controlled_buffer_13_out = decoder_1_out1 ? nor_27_out : 1'bz;  // Controlled_Buffer controlled_buffer_14
  nor nor_28 (nor_28_out, nor_27_out, and_32_out);
  nor nor_29 (nor_29_out, and_33_out, nor_30_out);
  assign controlled_buffer_13_out = decoder_1_out2 ? nor_29_out : 1'bz;  // Controlled_Buffer controlled_buffer_15
  nor nor_30 (nor_30_out, nor_29_out, and_34_out);
  nor nor_31 (nor_31_out, and_35_out, nor_32_out);
  assign controlled_buffer_13_out = decoder_1_out3 ? nor_31_out : 1'bz;  // Controlled_Buffer controlled_buffer_16
  nor nor_32 (nor_32_out, nor_31_out, and_36_out);
  LED led_4 (.in(controlled_buffer_13_out));
endmodule
