// Logisim project SequentialMultipler.circ as structural Verilog: 1 circuit, main circuit Multiplier
module Multiplier (
  input  [3:0] A,
  input  [1:0] in_2,
  input  [1:0] in_3,
  input  [1:0] in_4,
  input  [1:0] in_5,
  input  [1:0] in_6,
  input  [1:0] in_7,
  input  [1:0] in_8,
  input  [3:0] B,
  input  [2:0] in_10,
  input  [2:0] in_11,
  input  [2:0] in_12,
  output [7:0] PRODUCT
);

  wire bitselector_1_out, bitselector_2_out, bitselector_3_out, bitselector_4_out;
  wire [3:0] shifter_1_out, shifter_3_out, shifter_5_out;
  wire [7:0] adder_1_out, adder_2_out, and_1_out, and_2_out, and_3_out, and_4_out, bit_extender_1_out,
       bit_extender_2_out, bit_extender_3_out, bit_extender_4_out, bit_extender_5_out, shifter_2_out,
       shifter_4_out, shifter_6_out;

  assign bit_extender_1_out = {{4{1'b0}}, B};  // Bit_Extender bit_extender_1
  BitSelector #(.width(4)) bitselector_1 (.in(A), .out(bitselector_1_out), .sel(in_2));
  assign bit_extender_2_out = {{7{bitselector_1_out}}, bitselector_1_out};  // Bit_Extender bit_extender_2
  assign and_1_out = bit_extender_2_out & bit_extender_1_out;  // AND_Gate and_1, 8 bits wide
  Shifter #(.shift("lr"), .width(4)) shifter_1 (.in(A), .\dist (in_3), .out(shifter_1_out));
  BitSelector #(.width(4)) bitselector_2 (.in(shifter_1_out), .out(bitselector_2_out), .sel(in_6));
  Shifter shifter_2 (.in(bit_extender_1_out), .\dist (in_10), .out(shifter_2_out));
  assign bit_extender_3_out = {{7{bitselector_2_out}}, bitselector_2_out};  // Bit_Extender bit_extender_3
  Adder adder_1 (.a(and_1_out), .b(and_2_out), .out(adder_1_out));  // open: cin, cout
  assign and_2_out = bit_extender_3_out & shifter_2_out;  // AND_Gate and_2, 8 bits wide
  Shifter #(.shift("lr"), .width(4)) shifter_3 (.in(shifter_1_out), .\dist (in_4), .out(shifter_3_out));
  BitSelector #(.width(4)) bitselector_3 (.in(shifter_3_out), .out(bitselector_3_out), .sel(in_7));
  assign bit_extender_4_out = {{7{bitselector_3_out}}, bitselector_3_out};  // Bit_Extender bit_extender_4
  Shifter shifter_4 (.in(shifter_2_out), .\dist (in_11), .out(shifter_4_out));
  assign and_3_out = bit_extender_4_out & shifter_4_out;  // AND_Gate and_3, 8 bits wide
  Shifter #(.shift("lr"), .width(4)) shifter_5 (.in(shifter_3_out), .\dist (in_5), .out(shifter_5_out));
  BitSelector #(.width(4)) bitselector_4 (.in(shifter_5_out), .out(bitselector_4_out), .sel(in_8));
  Shifter shifter_6 (.in(shifter_4_out), .\dist (in_12), .out(shifter_6_out));
  Adder adder_2 (.a(adder_1_out), .b(and_3_out), .out(adder_2_out));  // open: cin, cout
  assign bit_extender_5_out = {{7{bitselector_4_out}}, bitselector_4_out};  // Bit_Extender bit_extender_5
  Adder adder_3 (.a(adder_2_out), .b(and_4_out), .out(PRODUCT));  // open: cin, cout
  assign and_4_out = bit_extender_5_out & shifter_6_out;  // AND_Gate and_4, 8 bits wide

  // Notes on the sheet:
  //   Multiplier
  //   Mulitplicand
  //   Elliot FORCIER-POIRIER, 260989602
endmodule
