// Logisim project led.circ as structural Verilog: 1 circuit, main circuit main
module main (
);

  wire and_1_out, and_2_out, and_3_out, and_4_out, and_5_out, and_6_out, and_7_out, and_8_out, and_9_out,
       clock_1_out, not_1_out, not_2_out, not_3_out, not_4_out, not_5_out, not_6_out, not_7_out, not_8_out,
       not_9_out, not_10_out, not_11_out, not_12_out, not_13_out, not_14_out, not_15_out, not_16_out,
       not_17_out, not_18_out, not_19_out, not_20_out, not_21_out, or_1_out, or_2_out, or_3_out, or_4_out,
       t_ff_1_q, t_ff_1_qn, t_ff_2_q, t_ff_2_qn, t_ff_3_q, t_ff_3_qn, t_ff_4_q, t_ff_4_qn;

  Clock #(.phaseOffset(1)) clock_1 (.out(clock_1_out));
  T_Flip_Flop t_ff_1 (.T(clock_1_out), .clk(clock_1_out), .Q(t_ff_1_q), .Qn(t_ff_1_qn));  // open: reset, preset
  T_Flip_Flop t_ff_2 (.T(t_ff_1_q), .clk(t_ff_1_q), .Q(t_ff_2_q), .Qn(t_ff_2_qn));  // open: reset, preset
  T_Flip_Flop t_ff_3 (.T(t_ff_2_q), .clk(t_ff_2_q), .Q(t_ff_3_q), .Qn(t_ff_3_qn));  // open: reset, preset
  T_Flip_Flop t_ff_4 (.T(t_ff_3_q), .clk(t_ff_3_q), .Q(t_ff_4_q), .Qn(t_ff_4_qn));  // open: reset, preset
  not not_1 (not_1_out, t_ff_4_qn);
  not not_2 (not_2_out, t_ff_1_qn);
  not not_3 (not_3_out, t_ff_4_qn);
  not not_4 (not_4_out, t_ff_2_qn);
  not not_5 (not_5_out, t_ff_4_qn);
  not not_6 (not_6_out, t_ff_2_qn);
  not not_7 (not_7_out, t_ff_3_qn);
  not not_8 (not_8_out, t_ff_4_qn);
  not not_9 (not_9_out, t_ff_1_qn);
  not not_10 (not_10_out, t_ff_2_qn);
  not not_11 (not_11_out, t_ff_3_qn);
  not not_12 (not_12_out, t_ff_4_qn);
  not not_13 (not_13_out, t_ff_1_qn);
  not not_14 (not_14_out, t_ff_2_qn);
  not not_15 (not_15_out, t_ff_4_qn);
  not not_16 (not_16_out, t_ff_1_qn);
  not not_17 (not_17_out, t_ff_3_qn);
  not not_18 (not_18_out, t_ff_4_qn);
  not not_19 (not_19_out, t_ff_3_qn);
  not not_20 (not_20_out, t_ff_4_qn);
  not not_21 (not_21_out, t_ff_4_q);
  and and_1 (and_1_out, t_ff_4_q, t_ff_1_qn, t_ff_2_qn, t_ff_3_qn, not_1_out);
  and and_2 (and_2_out, t_ff_4_q, not_2_out, t_ff_2_qn, t_ff_3_qn, not_3_out);
  and and_3 (and_3_out, t_ff_4_q, t_ff_1_qn, not_4_out, t_ff_3_qn, not_5_out);
  and and_4 (and_4_out, t_ff_4_q, t_ff_1_qn, not_6_out, not_7_out, not_8_out);
  and and_5 (and_5_out, t_ff_4_q, not_9_out, not_10_out, not_11_out, not_12_out);
  and and_6 (and_6_out, t_ff_4_q, not_13_out, not_14_out, t_ff_3_qn, not_15_out);
  and and_7 (and_7_out, t_ff_4_q, not_16_out, t_ff_2_qn, not_17_out, not_18_out);
  and and_8 (and_8_out, t_ff_4_q, t_ff_1_qn, t_ff_2_qn, not_19_out, not_20_out);
  and and_9 (and_9_out, not_21_out, t_ff_1_qn, t_ff_2_qn, t_ff_3_qn, t_ff_4_qn);
  or or_1 (or_1_out, and_3_out, and_5_out);
  or or_2 (or_2_out, and_6_out, and_7_out);
  or or_3 (or_3_out, and_2_out, and_4_out);
  LED led_1 (.in(or_3_out));
  LED led_2 ();  // open: in
  or or_4 (or_4_out, and_1_out, and_9_out);
  LED led_3 (.in(or_4_out));
  LED led_4 ();  // open: in
  LED led_5 ();  // open: in
  LED led_6 ();  // open: in
  LED led_7 (.in(or_1_out));
  LED led_8 ();  // open: in
  LED led_9 (.in(and_8_out));
  LED led_10 (.in(or_2_out));

  // Notes on the sheet:
  //   0
  //   1
  //   2
  //   3
  //   Elliot FORCIER-POIRIER, 260989602
  //   4
  //   5
  //   6
  //   7
  //   8
  //   9
endmodule
